# Fritzing sketch hb_final (saved by Fritzing 0.8.7b)
breadboards: 1

parts:
  M1 = DC Motor
  D1 = Rectifier Diode [part_number=1N4001 package="300 mil [THT]"]
  D2 = Rectifier Diode [part_number=1N4001 package="300 mil [THT]"]
  D3 = Rectifier Diode [part_number=1N4001 package="300 mil [THT]"]
  D4 = Rectifier Diode [part_number=1N4001 package="300 mil [THT]"]
  Q2 = NPN-Transistor [part_number=2N3904 package="TO92 [THT]"]
  Q4 = NPN-Transistor [part_number=2N3904 package="TO92 [THT]"]
  S1 = Pushbutton [package="[THT]"]
  S2 = Pushbutton [package="[THT]"]
  R1 = Resistor [tolerance=±5% resistance=330 package=THT]
  R2 = Resistor [tolerance=±5% resistance=330 package=THT]
  R3 = Resistor [tolerance=±5% resistance=330 package=THT]
  R4 = Resistor [tolerance=±5% resistance=330 package=THT]
  S3 = Pushbutton [package="[THT]"]
  S4 = Pushbutton [package="[THT]"]
  Q1 = PNP-Transistor [part_number=2N3906 package="TO92 [THT]"]
  Q3 = PNP-Transistor [part_number=2N3906 package="TO92 [THT]"]

nets:
  N1: M1.pin_1, D2.anode, D4.cathode, Q4.C, Q3.C
  N2: M1.pin_2, D1.anode, D3.cathode, Q2.C, Q1.C
  5V: D1.cathode, D2.cathode, S2.Pin_3, S2.Pin_4, S4.Pin_1, S4.Pin_2, Q1.E, Q3.E
  GND: D3.anode, D4.anode, Q2.E, Q4.E, S1.Pin_3, S1.Pin_4, S3.Pin_1, S3.Pin_2
  N3: Q2.B, R2.Pin_1
  N4: Q4.B, R4.Pin_0
  N5: S1.Pin_1, S1.Pin_2, R1.Pin_0
  N6: S2.Pin_1, S2.Pin_2, R2.Pin_0
  N7: R1.Pin_1, Q1.B
  N8: R3.Pin_0, Q3.B
  N9: R3.Pin_1, S3.Pin_3, S3.Pin_4
  N10: R4.Pin_1, S4.Pin_3, S4.Pin_4
