# Fritzing sketch circuit_1-1 (saved by Fritzing 0.8.7b)
breadboards: 1

parts:
  R2 = Resistor [tolerance=±5% resistance=1k package=THT]
  V1 = DC Power [voltage=5]

nets:
  N1: R2.Pin_0, V1.V-
  N2: R2.Pin_1, V1.V+
